// Digital circuit canis.dig as structural Verilog
module canis (
  input  clk
);

  wire [2:0] decoder_1_dsrc;
  wire [3:0] decoder_1_aluo;
  wire [15:0] add_1_s, addressspace_1_d, addressspace_1_i, alu_1_cry, alu_1_out, decoder_1_alua,
       decoder_1_alub, multiplexer_1_out, PC_q;

  Register #(.Bits(16), .generic("this.Bits=int(args.bits);")) PC (.D(add_1_s), .C(clk), .en(1'b1), .Q(PC_q));
  Add #(.Bits(16)) add_1 (.a(PC_q), .b(16'h1), .c_i(1'b0), .s(add_1_s));  // open: c_o
  addressSpace addressspace_1 (
    .C(clk), .Ia(PC_q), .Da({16{1'b0}}), .Din({16{1'b0}}), .str(1'b0), .I(addressspace_1_i),
    .D(addressspace_1_d));
  Multiplexer #(.Selector_Bits(3), .Bits(16)) multiplexer_1 (
    .sel(decoder_1_dsrc), .in_0(alu_1_out), .in_1(decoder_1_alub), .in_2(addressspace_1_d), .in_3(PC_q),
    .in_4(alu_1_cry), .in_5({16{1'b0}}), .in_6({16{1'b0}}), .in_7({16{1'b0}}), .out(multiplexer_1_out));
  decoder decoder_1 (
    .C(clk), .I(addressspace_1_i), .Din(multiplexer_1_out), .ALUa(decoder_1_alua), .ALUb(decoder_1_alub),
    .ALUo(decoder_1_aluo), .Dsrc(decoder_1_dsrc));
  alu alu_1 (.C(clk), .a(decoder_1_alua), .b(decoder_1_alub), .op(decoder_1_aluo), .out(alu_1_out), .cry(alu_1_cry));
endmodule
